# Fritzing sketch photoresistor_with_internal_pullup (saved by Fritzing 0.7.7b)
breadboards: 1

parts:
  Arduino1 = Arduino
  R1 = Photocell (LDR) [package=THT]

nets:
  N1: Arduino1.GND, R1.pin_0
  N2: Arduino1.A0, R1.pin_1
