# Fritzing sketch pushbutton_with_internal_pullup (saved by Fritzing 0.7.7b)
breadboards: 1

parts:
  Arduino1 = Arduino
  S1 = Pushbutton [package="[THT]"]

nets:
  N1: Arduino1.GND, S1.Pin_3, S1.Pin_4
  N2: Arduino1.D2, S1.Pin_1, S1.Pin_2
