# Fritzing sketch TestBoardWiring (saved by Fritzing 0.7.7b)
breadboards: 1

parts:
  LED1 = LED - 5mm [color="Red (633nm)" package="5 mm [THT]"]
  Arduino1 = Arduino
  S1 = Pushbutton [package="[THT]"]
  LED2 = LED - 5mm [color="Green (560nm)" package="5 mm [THT]"]
  R1 = Resistor [tolerance=±5% resistance=220 package=THT]
  R2 = Resistor [tolerance=±5% resistance=220 package=THT]
  R3 = Resistor [tolerance=±5% resistance=220 package=THT]

nets:
  N1: LED1.cathode, Arduino1.D7, R1.Pin_1
  N2: Arduino1.GND, R1.Pin_0, R2.Pin_0
  N3: Arduino1.D9, Arduino1.A0
  N4: Arduino1.D8, S1.Pin_1, S1.Pin_2, R3.Pin_1
  N5: Arduino1.D6, LED2.anode
  N6: S1.Pin_3, S1.Pin_4
  N7: LED2.cathode, R2.Pin_1
